// Logisim project exp 9.circ as structural Verilog: 1 circuit, main circuit main
module main (
  input  [2:0] S0_S1_S2,
  input  Binvert,
  input  A,
  input  Cin,
  input  B,
  output Y,
  output Cout
);

  wire adder_1_out, and_1_out, and_2_out, and_3_out, not_1_out, not_2_out, or_1_out, or_2_out, xor_1_out;

  not not_1 (not_1_out, B);
  and and_1 (and_1_out, B, Binvert);
  and and_2 (and_2_out, not_1_out, Binvert);
  or or_1 (or_1_out, and_1_out, and_2_out);
  not not_2 (not_2_out, A);
  and and_3 (and_3_out, A, or_1_out);
  or or_2 (or_2_out, A, or_1_out);
  xor xor_1 (xor_1_out, A, or_1_out);
  Adder #(.width(1)) adder_1 (.a(A), .b(or_1_out), .out(adder_1_out), .cin(Cin), .cout(Cout));
  Multiplexer #(.select(3), .enable("false")) multiplexer_1 (
    .in0(not_2_out), .in1(and_3_out), .in2(or_2_out), .in3(xor_1_out), .in5(adder_1_out), .out(Y),
    .sel(S0_S1_S2));  // open: in4, in6, in7
endmodule
